// Logisim project 8-bit Data path.circ as structural Verilog: 1 circuit, main circuit main
module main (
  input  [1:0] Write_addr,
  input  Write_enable,
  input  [1:0] Read_addr_A,
  input  [1:0] Read_addr_B,
  input  [2:0] in_5,
  output [3:0] out_6
);

  wire clock_1_out;
  wire [7:0] main_1_out_a, main_1_out_b, main_2_p4;

  Clock clock_1 (.out(clock_1_out));
  Register_main main_1 (
    .Data_In(main_2_p4), .Write_Address(Write_addr), .Write_Enable(Write_enable), .Clock(clock_1_out),
    .Out_A(main_1_out_a), .Out_B(main_1_out_b), .Read_Addr_A(Read_addr_A), .Read_Addr_B(Read_addr_B));
  // ALU_main main_2: pin names not known; wires that end beside it: main_1_out_a, main_1_out_b, in_5, main_2_p4, out_6
endmodule
