// Logisim project Instruction Register.circ as structural Verilog: 1 circuit, main circuit main
module main (
);

  wire [7:0] main_1_memory_addr__to_read;

  Program_Counter_main main_1 (.Memory_Addr__to_read(main_1_memory_addr__to_read));  // open: Jump_Address, Jump_Enable, Clock, Reset
  ROM rom_1 (.addr(main_1_memory_addr__to_read));  // open: data, sel
endmodule
