// Logisim project Program Counter.circ as structural Verilog: 1 circuit, main circuit main
module main (
  input  [7:0] Jump_Address,
  input  Reset,
  input  Jump_Enable,
  input  Clock,
  output [7:0] Memory_Addr__to_read
);

  wire [7:0] adder_1_out, multiplexer_1_out;

  Adder adder_1 (.a(Memory_Addr__to_read), .b(8'h1), .out(adder_1_out));  // open: cin, cout
  Multiplexer #(.width(8)) multiplexer_1 (
    .in0(adder_1_out), .in1(Jump_Address), .out(multiplexer_1_out), .sel(Jump_Enable));  // open: en
  Register register_1 (.D(multiplexer_1_out), .Q(Memory_Addr__to_read), .clk(Clock), .clr(Reset));  // open: en
endmodule
