// Logisim project Register.circ as structural Verilog: 1 circuit, main circuit main
module main (
  input  [7:0] Data_In,
  input  [1:0] Write_Address,
  input  [1:0] Read_Addr_A,
  input  Write_Enable,
  input  Clock,
  input  [1:0] Read_Addr_B,
  output [7:0] Out_A,
  output [7:0] Out_B
);

  wire decoder_1_out0, decoder_1_out1, decoder_1_out2, decoder_1_out3;
  wire [7:0] _0_q, _1_q, _2_q, _3_q;

  Decoder #(.select(2), .disabled(0)) decoder_1 (
    .out0(decoder_1_out0), .out1(decoder_1_out1), .out2(decoder_1_out2), .out3(decoder_1_out3),
    .sel(Write_Address), .en(Write_Enable));
  Register _0 (.D(Data_In), .en(decoder_1_out0), .Q(_0_q), .clk(Clock));  // open: clr
  Register _2 (.D(Data_In), .en(decoder_1_out2), .Q(_2_q), .clk(Clock));  // open: clr
  Register _1 (.D(Data_In), .en(decoder_1_out1), .Q(_1_q), .clk(Clock));  // open: clr
  Register _3 (.D(Data_In), .en(decoder_1_out3), .Q(_3_q), .clk(Clock));  // open: clr
  Multiplexer #(.select(2), .width(8), .enable("false")) multiplexer_1 (
    .in0(_0_q), .in1(_1_q), .in2(_2_q), .in3(_3_q), .out(Out_A), .sel(Read_Addr_A));
  Multiplexer #(.select(2), .width(8), .enable("false")) multiplexer_2 (
    .in0(_0_q), .in1(_1_q), .in2(_2_q), .in3(_3_q), .out(Out_B), .sel(Read_Addr_B));

  // Notes on the sheet:
  //   Didnt use DMUX as its hardware inefficient
endmodule
